// Logisim project instruction_execution.circ as structural Verilog: 1 circuit, main circuit main
module main (
  output [15:0] out_1,
  output [3:0] Reg_Addr
);

  wire and_2_out, button_1_out, d_ff_1_q, d_ff_2_q, decoder_1_out0, decoder_1_out1, decoder_1_out2,
       decoder_1_out3, decoder_1_out4, decoder_1_out5, decoder_1_out6, decoder_1_out7, decoder_1_out8,
       decoder_1_out9, decoder_1_out10, decoder_1_out11, decoder_1_out12, decoder_1_out13, decoder_1_out14,
       decoder_1_out15, decoder_2_out0, decoder_2_out1, decoder_2_out2, decoder_2_out3, decoder_2_out4,
       decoder_2_out5, decoder_2_out6, decoder_2_out7, decoder_2_out8, decoder_2_out9, decoder_2_out10,
       decoder_2_out11, decoder_2_out12, decoder_2_out13, decoder_2_out14, decoder_2_out15,
       demultiplexer_1_out0, demultiplexer_1_out1, j_k_ff_1_q, Main_Clock_out, not_1_out,
       pull_resistor_1_node, undriven, undriven_2, xor_1_out;
  wire [7:0] multiplexer_1_out, PRogram_Counter_q, ram_1_data, register_1_q, register_2_q, register_3_q,
       register_4_q, register_5_q, register_6_q, register_7_q;

  Button button_1 (.out(button_1_out));
  RAM ram_1 (.addr(PRogram_Counter_q), .data(ram_1_data), .sel(1'b1), .clk(button_1_out));  // open: ld, clr
  Shift_Register #(.length(1)) shift_register_1 (
    .shift(undriven), .in(ram_1_data[0]), .clk(demultiplexer_1_out0), .out(out_1[15]));  // open: load, clr, d0, q0
  Shift_Register #(.length(1)) shift_register_2 (
    .shift(undriven), .in(ram_1_data[1]), .clk(demultiplexer_1_out0), .out(out_1[14]));  // open: load, clr, d0, q0
  Shift_Register #(.length(1)) shift_register_3 (
    .shift(undriven), .in(ram_1_data[2]), .clk(demultiplexer_1_out0), .out(out_1[13]));  // open: load, clr, d0, q0
  Shift_Register #(.length(1)) shift_register_4 (
    .shift(undriven), .in(ram_1_data[3]), .clk(demultiplexer_1_out0), .out(out_1[12]));  // open: load, clr, d0, q0
  Shift_Register #(.length(1)) shift_register_5 (
    .shift(undriven), .in(ram_1_data[4]), .clk(demultiplexer_1_out0), .out(out_1[11]));  // open: load, clr, d0, q0
  Shift_Register #(.length(1)) shift_register_6 (
    .shift(undriven), .in(ram_1_data[5]), .clk(demultiplexer_1_out0), .out(out_1[10]));  // open: load, clr, d0, q0
  Shift_Register #(.length(1)) shift_register_7 (
    .shift(undriven), .in(ram_1_data[6]), .clk(demultiplexer_1_out0), .out(out_1[9]));  // open: load, clr, d0, q0
  Shift_Register #(.length(1)) shift_register_8 (
    .shift(undriven), .in(ram_1_data[7]), .clk(demultiplexer_1_out0), .out(out_1[8]));  // open: load, clr, d0, q0
  xor xor_1 (xor_1_out, d_ff_1_q, 1'b1);
  D_Flip_Flop d_ff_1 (.clk(demultiplexer_1_out0), .D(xor_1_out), .Q(d_ff_1_q));  // open: Qn, preset, en, reset
  Shift_Register #(.length(1)) shift_register_9 (
    .shift(undriven_2), .in(out_1[15]), .clk(demultiplexer_1_out0), .out(out_1[7]));  // open: load, clr, d0, q0
  Shift_Register #(.length(1)) shift_register_10 (
    .shift(undriven_2), .in(out_1[14]), .clk(demultiplexer_1_out0), .out(out_1[6]));  // open: load, clr, d0, q0
  Shift_Register #(.length(1)) shift_register_11 (
    .shift(undriven_2), .in(out_1[13]), .clk(demultiplexer_1_out0), .out(out_1[5]));  // open: load, clr, d0, q0
  Shift_Register #(.length(1)) shift_register_12 (
    .shift(undriven_2), .in(out_1[12]), .clk(demultiplexer_1_out0), .out(out_1[4]));  // open: load, clr, d0, q0
  Shift_Register #(.length(1)) shift_register_13 (
    .shift(undriven_2), .in(out_1[11]), .clk(demultiplexer_1_out0), .out(out_1[3]));  // open: load, clr, d0, q0
  Shift_Register #(.length(1)) shift_register_14 (
    .shift(undriven_2), .in(out_1[10]), .clk(demultiplexer_1_out0), .out(out_1[2]));  // open: load, clr, d0, q0
  Shift_Register #(.length(1)) shift_register_15 (
    .shift(undriven_2), .in(out_1[9]), .clk(demultiplexer_1_out0), .out(out_1[1]));  // open: load, clr, d0, q0
  Shift_Register #(.length(1)) shift_register_16 (
    .shift(undriven_2), .in(out_1[8]), .clk(demultiplexer_1_out0), .out(out_1[0]));  // open: load, clr, d0, q0
  D_Flip_Flop d_ff_2 (.clk(demultiplexer_1_out0), .D(d_ff_1_q), .Q(d_ff_2_q));  // open: Qn, preset, en, reset
  Pull_Resistor pull_resistor_1 (.node(pull_resistor_1_node));
  Decoder #(.select(4), .disabled(0)) decoder_1 (
    .out0(decoder_1_out0), .out1(decoder_1_out1), .out2(decoder_1_out2), .out3(decoder_1_out3),
    .out4(decoder_1_out4), .out5(decoder_1_out5), .out6(decoder_1_out6), .out7(decoder_1_out7),
    .out8(decoder_1_out8), .out9(decoder_1_out9), .out10(decoder_1_out10), .out11(decoder_1_out11),
    .out12(decoder_1_out12), .out13(decoder_1_out13), .out14(decoder_1_out14), .out15(decoder_1_out15),
    .sel(out_1[3:0]));  // open: en
  Clock Main_Clock (.out(Main_Clock_out));
  Demultiplexer demultiplexer_1 (
    .out0(demultiplexer_1_out0), .out1(demultiplexer_1_out1), .in(Main_Clock_out), .sel(j_k_ff_1_q));  // open: en
  J_K_Flip_Flop #(.trigger("falling")) j_k_ff_1 (
    .J(d_ff_2_q), .clk(Main_Clock_out), .K(pull_resistor_1_node), .Q(j_k_ff_1_q));  // open: Qn, preset, en, reset
  Pull_Resistor pull_resistor_2 (.node(pull_resistor_1_node));
  and and_1 (pull_resistor_1_node, demultiplexer_1_out1, decoder_1_out0);
  and and_2 (and_2_out, decoder_1_out1, demultiplexer_1_out1);
  and and_3 (pull_resistor_1_node, decoder_1_out1, and_2_out);
  Decoder #(.select(4)) decoder_2 (
    .out0(decoder_2_out0), .out1(decoder_2_out1), .out2(decoder_2_out2), .out3(decoder_2_out3),
    .out4(decoder_2_out4), .out5(decoder_2_out5), .out6(decoder_2_out6), .out7(decoder_2_out7),
    .out8(decoder_2_out8), .out9(decoder_2_out9), .out10(decoder_2_out10), .out11(decoder_2_out11),
    .out12(decoder_2_out12), .out13(decoder_2_out13), .out14(decoder_2_out14), .out15(decoder_2_out15),
    .sel(out_1[7:4]), .en(decoder_1_out1));
  Pull_Resistor pull_resistor_3 (.node(and_2_out));
  Pull_Resistor pull_resistor_4 (.node(decoder_2_out0));
  not not_1 (not_1_out, decoder_2_out0);
  and and_4 (demultiplexer_1_out0, decoder_2_out0, and_2_out);
  Register register_1 (.D(out_1[15:8]), .en(decoder_2_out1), .Q(register_1_q), .clk(and_2_out));  // open: clr
  Register register_2 (.D(out_1[15:8]), .en(decoder_2_out2), .Q(register_2_q), .clk(and_2_out));  // open: clr
  Register register_3 (.D(out_1[15:8]), .en(decoder_2_out3), .Q(register_3_q), .clk(and_2_out));  // open: clr
  Register register_4 (.D(out_1[15:8]), .en(decoder_2_out4), .Q(register_4_q), .clk(and_2_out));  // open: clr
  Register register_5 (.D(out_1[15:8]), .en(decoder_2_out5), .Q(register_5_q), .clk(and_2_out));  // open: clr
  Register register_6 (.D(out_1[15:8]), .en(decoder_2_out6), .Q(register_6_q), .clk(and_2_out));  // open: clr
  Register register_7 (.D(out_1[15:8]), .en(decoder_2_out7), .Q(register_7_q), .clk(and_2_out));  // open: clr
  Counter #(.trigger("falling")) PRogram_Counter (
    .load(decoder_2_out0), .D(out_1[15:8]), .count(not_1_out), .Q(PRogram_Counter_q),
    .clk(demultiplexer_1_out0));  // open: carry, clr
  Multiplexer #(.select(4), .width(8)) multiplexer_1 (
    .in0(register_7_q), .in1(register_6_q), .in2(register_5_q), .in3(register_4_q), .in4(register_3_q),
    .in5(register_2_q), .in6(register_1_q), .in7(PRogram_Counter_q), .out(multiplexer_1_out), .sel(out_1[7:4]));  // open: in8, in9, in10, in11, in12, in13, in14, in15, en

  assign Reg_Addr = out_1[7:4];

  // Notes on the sheet:
  //   Delay 2 cycles 
  //   Instruction Ready
  //   Data
  //   NC. 0xF = HALT
  //   Op Code
  //   Instruction End
  //   NOP
  //   and_1 drives only 1 and floats otherwise
  //   LOADI
  //   Instruction Clock
  //   and_3 drives only 1 and floats otherwise
  //   Read Data
  //   Increment CLK
  //   Write Data
  //   Write CLK
  //   Write EN
  //   and_4 drives only 1 and floats otherwise
endmodule
